// Logisim project LEDTrafficLights_logisim.circ as structural Verilog: 1 circuit, main circuit main
module main (
);

  wire button_1_out, clock_1_out;
  wire [1:0] rom_2_data;
  wire [2:0] rom_1_data;
  wire [3:0] counter_1_q, counter_2_q;

  Clock clock_1 (.out(clock_1_out));
  Counter #(.width(4), .max('hf)) counter_1 (
    .count(clock_1_out), .Q(counter_1_q), .clk(clock_1_out), .clr(button_1_out));  // open: load, D, carry
  Button button_1 (.out(button_1_out));
  Counter #(.width(4), .max('hf)) counter_2 (
    .count(clock_1_out), .Q(counter_2_q), .clk(clock_1_out), .clr(button_1_out));  // open: load, D, carry
  ROM #(.addrWidth(4), .dataWidth(3)) rom_1 (.addr(counter_1_q), .data(rom_1_data));  // open: sel
  ROM #(.addrWidth(4), .dataWidth(2)) rom_2 (.addr(counter_2_q), .data(rom_2_data));  // open: sel
  LED led_1 (.in(rom_2_data[0]));
  LED led_2 (.in(rom_2_data[1]));
  LED led_3 (.in(rom_1_data[0]));
  LED led_4 (.in(rom_1_data[0]));
  LED led_5 (.in(rom_1_data[0]));
  LED led_6 (.in(rom_1_data[1]));
  LED led_7 (.in(rom_1_data[1]));
  LED led_8 (.in(rom_1_data[1]));
  LED led_9 (.in(rom_1_data[2]));
  LED led_10 (.in(rom_1_data[2]));
  LED led_11 (.in(rom_1_data[2]));

  // Notes on the sheet:
  //   contents of rom_1 (hex, n*v repeats v):
  //   2 2 5*1 2 2 2 6*4
  //   contents of rom_2 (hex, n*v repeats v):
  //   10*3
endmodule
